# Fritzing sketch ZHSG (saved by Fritzing 0.8.7b)
circuit board: 8.46667cm x 5.64444cm
breadboards: 1

parts:
  Arduino = Arduino Uno (Rev3)
  U1 = Optocoupler [package=THT]
  LCD1 = LCD screen
  U2 = Voltage Regulator - 5V [package="TO220 [THT]"]
  R2 = Resistor [tolerance=±5% resistance=4.7k package=THT]
  U3 = Optocoupler [package=THT]
  R4 = Resistor [tolerance=±5% resistance=4.7k package=THT]
  LM4040CIZ-5_0-NOPB = TRANSISTOR_NPN [package=to-92]
  R5 = Resistor [tolerance=±5% resistance=540 package=THT]
  R6 = Resistor [tolerance=±5% resistance=22k package=THT]
  R7 = Resistor [tolerance=±5% resistance=47k package=THT]
  R8 = Resistor [tolerance=±5% resistance=22k package=THT]
  R9 = Resistor [tolerance=±5% resistance=47k package=THT]
  R10 = Resistor [tolerance=±5% resistance=4.7k package=THT]
  R11 = Resistor [tolerance=±5% resistance=4.7k package=THT]
  Q1 = MOSFET-NCHANNEL [package=to-92]
  Out = screw terminal, 5 pins
  R12 = Trimmer Potentiometer [maximum_resistance=10kΩ package=THT]
  R13 = Trimmer Potentiometer [maximum_resistance=10kΩ package=THT]
  R14 = Resistor [tolerance=±5% resistance=1k package=THT]
  C1 = Electrolytic Capacitor [capacitance=4.7µF package="100 mil [THT, electrolytic]"]
  C2 = Electrolytic Capacitor [capacitance=4.7µF package="100 mil [THT, electrolytic]"]
  L1 = Inductor [inductance=8.7 current=1.5 package="400 mil [THT]"]
  R15 = Resistor [tolerance=±5% resistance=220 package=THT]
  R16 = Resistor [tolerance=±5% resistance=100 package=THT]
  IN = screw terminal, 7 pins
  R17 = Trimmer Potentiometer [maximum_resistance=10kΩ package=THT]
  J2 = longpad pin header, 2 pins [form="long pad"]
  J1 = longpad pin header, 5 pins [form="long pad"]

nets:
  N1: Arduino.A0, R6.Pin_1, R7.Pin_0
  N2: Arduino.A1, R8.Pin_1, R9.Pin_0
  N3: Arduino.A2, IN.pin6
  N4: Arduino.D8, R14.Pin_0
  N5: Arduino.D11_PWM/MOSI, U3.Pin_5, R4.Pin_1
  N6: Arduino.D12/MISO, U1.Pin_5, R2.Pin_1
  GND: Arduino.GND, U1.Pin_2, U1.Pin_4, LCD1.VSS, LCD1.R/W, LCD1.LED-, U2.GND, U3.Pin_2, U3.Pin_4, LM4040CIZ-5_0-NOPB.E, R12.wiper, R13.wiper, C1.-, C2.-, R15.Pin_1, IN.pin7, R17.leg1
  N7: Arduino.AREF, LM4040CIZ-5_0-NOPB.B, R5.Pin_1
  N8: Arduino.D2, LCD1.RS
  N9: Arduino.D3_PWM, LCD1.E
  N10: Arduino.D4, LCD1.DB4
  N11: Arduino.D5_PWM, LCD1.DB5
  N12: Arduino.D6_PWM, LCD1.DB6
  N13: Arduino.D7, LCD1.DB7
  5V: Arduino.5V, LCD1.VDD, U2.output_voltage, R5.Pin_0, R17.leg2
  N14: U1.Pin_1, R10.Pin_1
  N15: LCD1.V0, R17.wiper
  N16: LCD1.LED+, R15.Pin_0, R16.Pin_0
  N17: U2.input_voltage, C2.+, L1.pin_1
  N18: R2.Pin_0, R4.Pin_0, R8.Pin_0, C1.+, L1.pin_0, IN.pin1, J1.pin1
  N19: U3.Pin_1, R11.Pin_1
  N20: R6.Pin_0, IN.pin2, J1.pin2
  N21: R7.Pin_1, R12.leg2
  N22: R9.Pin_1, R13.leg2
  N23: R10.Pin_0, IN.pin3, J1.pin3
  N24: R11.Pin_0, IN.pin4, J1.pin4
  N25: Q1.S, Out.pin1, J2.pin1
  N26: Q1.G, R14.Pin_1
  N27: R16.Pin_1, IN.pin5, J1.pin5

notes:
  Spannungsmessung Batt. 1
  Spannungsmessung Batt. 2
  12 V Zweitbatterie
  GND
  Zündung
  Zuheizer
  12 V Hauptbatterie
  Trennrelais
  Zuheizer Steuergerät
  Amaturenbel
  4,5V / 45mA
  Debug Inputs
  Temp Kühlwasser
  Spannungsreferenz
  Vcc
  Pin 7 GND
  Pin 6 Temp Kühlwasser
  Pin 5 Amaturenbeleuchtung
  Pin 4 Zündung
  Pin 3 Zuheizer Uhr
  Pin 2 12V Hauptbatterie
  Pin 1 12V Zweitbatterie
